# Fritzing sketch Capstone Draw (saved by Fritzing 0.9.3b)

parts:
  SIM_800A = SIM800L [package=THT]
  U1 = RELAY [package=relay-jzc]
  Power = Power Jack [package=power_jack_smd]
  U2 = HALL-EFFECT [package=sc70]
  Part3 = Arduino Mega 2560 (Rev3)
  DS1307 = Real Time Clock Module - DS1307 RTC Breakout Board

nets:
  5V: SIM_800A.5V, Part3.VIN
  GND: SIM_800A.GND#1, U1.COIL2, U2.GND, Part3.GND, DS1307.GND
  N1: SIM_800A.VDD, Power.GNDBREAK
  N2: SIM_800A.SIM_TXD, Part3.D50
  N3: SIM_800A.SIM_RXD, Part3.D51
  N4: SIM_800A.GND#5, SIM_800A.RST, Power.GND
  N5: U1.COIL1, Part3.D12_PWM
  5V_2: U2.VCC, Part3.5V, DS1307.5V
  N6: U2.OUT, Part3.D11_PWM
  N7: Part3.D21/SCL, DS1307.SCL
  N8: Part3.D20/SDA, DS1307.SDA
